# Fritzing sketch 2Xbutton1xpot (saved by Fritzing 0.9.2b)
breadboards: 1

parts:
  Part1 = Arduino Uno (Rev3)
  S5 = Pushbutton [package=THT]
  S6 = Pushbutton [package=THT]
  R1 = Resistor [tolerance=±5% resistance=10k package="0603 [SMD]"]
  R6 = Resistor [tolerance=±5% resistance=10k package="0603 [SMD]"]
  R7 = Rotary Potentiometer (Small) [maximum_resistance=100kΩ package=THT]

nets:
  N1: Part1.A0, R7.wiper
  N2: Part1.D2, S6.leg1, R6.Pin_0
  N3: Part1.D3_PWM, S5.leg1, R1.Pin_0
  N4: Part1.5V, S5.leg0, S6.leg0, R7.leg2
  N5: Part1.GND, R1.Pin_1, R6.Pin_1, R7.leg1
