# Fritzing sketch huzzah32SensorSwitchBox Alt2-schematic (saved by Fritzing 0.9.3b)
stripboards: 1

parts:
  DIN = DIN-5 jack (MIDI) [package=THT]
  Part2 = Adafruit HUZZAH32 ESP32 Feather [part_number="Adafruit #3405"]
  R22 = Resistor [tolerance=±5% resistance=10k package="0402 [SMD]"]
  U1 = SWITCH_SPDT [package=kps-1290]
  R24 = Resistor [tolerance=±5% resistance=100 package="2010 [SMD]"]
  R25 = Resistor [tolerance=±5% resistance=22 package="2010 [SMD]"]
  R26 = Resistor [tolerance=±5% resistance=22 package="2010 [SMD]"]
  R27 = Resistor [tolerance=±5% resistance=10k package="0402 [SMD]"]
  LED1 = RGB LED (com. anode, rbg) [package="5 mm [THT]"]
  DIN_2 = DIN-5 jack (MIDI) [package=THT]
  R28 = Resistor [tolerance=±5% resistance=10k package="0402 [SMD]"]
  DIN1 = DIN-5 jack (MIDI) [package=THT]
  DIN2 = DIN-5 jack (MIDI) [package=THT]
  R29 = Resistor [tolerance=±5% resistance=10k package="0402 [SMD]"]
  R30 = Resistor [tolerance=±5% resistance=10k package="0402 [SMD]"]
  DIN_3 = DIN-5 jack (MIDI) [package=THT]
  R31 = Resistor [tolerance=±5% resistance=10k package="0402 [SMD]"]
  AMPHENOL_-_ACJS-MHDR_-_JACK_6_35MM7 = AMPHENOL - ACJS-MHDR [package=ACJS-MHDR]
  AMPHENOL_-_ACJS-MHDR_-_JACK_6_35MM8 = AMPHENOL - ACJS-MHDR [package=ACJS-MHDR]
  R32 = Resistor [tolerance=±5% resistance=10k package="0402 [SMD]"]
  AMPHENOL_-_ACJS-MHDR_-_JACK_6_35MM9 = AMPHENOL - ACJS-MHDR [package=ACJS-MHDR]
  R33 = Resistor [tolerance=±5% resistance=10k package="0402 [SMD]"]
  AMPHENOL_-_ACJS-MHDR_-_JACK_6_35MM10 = AMPHENOL - ACJS-MHDR [package=ACJS-MHDR]
  AMPHENOL_-_ACJS-MHDR_-_JACK_6_35MM11 = AMPHENOL - ACJS-MHDR [package=ACJS-MHDR]
  AMPHENOL_-_ACJS-MHDR_-_JACK_6_35MM12 = AMPHENOL - ACJS-MHDR [package=ACJS-MHDR]
  R34 = Resistor [tolerance=±5% resistance=10k package="0402 [SMD]"]
  R35 = Resistor [tolerance=±5% resistance=10k package="0402 [SMD]"]
  R36 = Resistor [tolerance=±5% resistance=10k package="0402 [SMD]"]
  LiPo_BAT = Battery Holders [package=lipo-1100mAh]

nets:
  A3: DIN.2, Part2.A3_I39, R27.Pin_1
  3.3V: DIN.4, Part2.3.3V, LED1.common_anode, DIN_2.4, DIN1.4, DIN2.4, DIN_3.4, AMPHENOL_-_ACJS-MHDR_-_JACK_6_35MM7.Tip_(3), AMPHENOL_-_ACJS-MHDR_-_JACK_6_35MM8.Tip_(3), AMPHENOL_-_ACJS-MHDR_-_JACK_6_35MM9.Tip_(3), AMPHENOL_-_ACJS-MHDR_-_JACK_6_35MM10.Tip_(3), AMPHENOL_-_ACJS-MHDR_-_JACK_6_35MM11.Tip_(3), LiPo_BAT.+
  GND: DIN.GND, Part2.GND, R22.Pin_1, U1.P, R27.Pin_0, DIN_2.GND, R28.Pin_0, DIN1.GND, DIN2.GND, R29.Pin_0, R30.Pin_0, DIN_3.GND, R31.Pin_0, R32.Pin_1, R33.Pin_1, R34.Pin_1, R35.Pin_1, R36.Pin_1
  N1: Part2.A5_IO4, R25.Pin_1
  A4: Part2.A4_IO36, DIN_2.2, R28.Pin_1
  A2: Part2.A2_I34, DIN_3.2, R31.Pin_1
  N2: Part2.A1_DAC1, R26.Pin_1
  N3: Part2.A0_DAC2, R24.Pin_1
  13: Part2.IO13_A12, AMPHENOL_-_ACJS-MHDR_-_JACK_6_35MM12.Sleeve_(1), R35.Pin_0
  27: Part2.IO27_A10, AMPHENOL_-_ACJS-MHDR_-_JACK_6_35MM11.Sleeve_(1), R36.Pin_0
  A9: Part2.IO33_A9, DIN1.2, R29.Pin_1
  15: Part2.IO15_A8, AMPHENOL_-_ACJS-MHDR_-_JACK_6_35MM10.Sleeve_(1), R34.Pin_0
  A7: Part2.IO32_A7, DIN2.2, R30.Pin_1
  14: Part2.IO14_A6, AMPHENOL_-_ACJS-MHDR_-_JACK_6_35MM9.Sleeve_(1), R33.Pin_0
  22: Part2.SCL, AMPHENOL_-_ACJS-MHDR_-_JACK_6_35MM8.Sleeve_(1), R32.Pin_0
  23: Part2.SDA, R22.Pin_0, AMPHENOL_-_ACJS-MHDR_-_JACK_6_35MM7.Sleeve_(1)
  N4: U1.O, LiPo_BAT.-
  N5: R24.Pin_0, LED1.red_cathode
  N6: R25.Pin_0, LED1.green_cathode
  N7: R26.Pin_0, LED1.blue_cathode

notes:
  NB - Currently you can not use WiFi and do an analogRead on any pin below 32, i.e. use A2, A3, A4​, A7, A9
  byte buttons[] = {23, 22, 14, 15, 27, 13};
  12 - This is GPIO #12 and also an analog input A11. This pin has a pull-down resistor built into it, we recommend using it as an output only, or making sure that the pull-down is not affected during boot.
  byte faders[] = {A2, A3, A4, A9, A7};
  17 cols x 18 rows
  Using a common anode RGB LED so connected to +. If using common cathode connect to GND and reverse HIGH and LOW in code.
