# Fritzing sketch huzzah32SensorSwitchBox Alt2 (saved by Fritzing 0.9.3b)
stripboards: 1

parts:
  AMPHENOL_-_ACJS-MHDR_-_JACK_6_35MM1 = AMPHENOL - ACJS-MHDR [package=ACJS-MHDR]
  AMPHENOL_-_ACJS-MHDR_-_JACK_6_35MM3 = AMPHENOL - ACJS-MHDR [package=ACJS-MHDR]
  AMPHENOL_-_ACJS-MHDR_-_JACK_6_35MM4 = AMPHENOL - ACJS-MHDR [package=ACJS-MHDR]
  AMPHENOL_-_ACJS-MHDR_-_JACK_6_35MM5 = AMPHENOL - ACJS-MHDR [package=ACJS-MHDR]
  AMPHENOL_-_ACJS-MHDR_-_JACK_6_35MM6 = AMPHENOL - ACJS-MHDR [package=ACJS-MHDR]
  AMPHENOL_-_ACJS-MHDR_-_JACK_6_35MM7 = AMPHENOL - ACJS-MHDR [package=ACJS-MHDR]
  DIN1 = DIN-5 jack (MIDI) [package=THT]
  DIN2 = DIN-5 jack (MIDI) [package=THT]
  DIN3 = DIN-5 jack (MIDI) [package=THT]
  DIN4 = DIN-5 jack (MIDI) [package=THT]
  DIN5 = DIN-5 jack (MIDI) [package=THT]
  Part2 = Adafruit HUZZAH32 ESP32 Feather [part_number="Adafruit #3405"]
  R18 = Resistor [tolerance=±5% resistance=10k package="0402 [SMD]"]
  R19 = Resistor [tolerance=±5% resistance=10k package="0402 [SMD]"]
  R20 = Resistor [tolerance=±5% resistance=10k package="0402 [SMD]"]
  R21 = Resistor [tolerance=±5% resistance=10k package="0402 [SMD]"]
  R22 = Resistor [tolerance=±5% resistance=10k package="0402 [SMD]"]
  R23 = Resistor [tolerance=±5% resistance=10k package="0402 [SMD]"]
  LED1 = RGB LED (com. cathode, rgb) [package="5 mm [THT]"]
  U1 = SWITCH_SPDT [package=kps-1290]  # not connected
  Part3 = Lithium Ion Polymer Battery 3.7v 500mAh [part_number=1578]  # not connected
  R24 = Resistor [tolerance=±5% resistance=100 package="2010 [SMD]"]
  R25 = Resistor [tolerance=±5% resistance=22 package="2010 [SMD]"]
  R26 = Resistor [tolerance=±5% resistance=22 package="2010 [SMD]"]
  R27 = Resistor [tolerance=±5% resistance=10k package="0402 [SMD]"]
  R28 = Resistor [tolerance=±5% resistance=10k package="0402 [SMD]"]
  R29 = Resistor [tolerance=±5% resistance=10k package="0402 [SMD]"]
  R30 = Resistor [tolerance=±5% resistance=10k package="0402 [SMD]"]
  R31 = Resistor [tolerance=±5% resistance=10k package="0402 [SMD]"]

nets:
  N1: AMPHENOL_-_ACJS-MHDR_-_JACK_6_35MM1.Sleeve_(4), Part2.IO13_A12, R18.Pin_0
  N2: AMPHENOL_-_ACJS-MHDR_-_JACK_6_35MM1.Tip_(6), AMPHENOL_-_ACJS-MHDR_-_JACK_6_35MM3.Tip_(3), AMPHENOL_-_ACJS-MHDR_-_JACK_6_35MM3.Tip_(6), AMPHENOL_-_ACJS-MHDR_-_JACK_6_35MM4.Tip_(6), AMPHENOL_-_ACJS-MHDR_-_JACK_6_35MM5.Tip_(3), AMPHENOL_-_ACJS-MHDR_-_JACK_6_35MM5.Tip_(6), AMPHENOL_-_ACJS-MHDR_-_JACK_6_35MM6.Tip_(6), AMPHENOL_-_ACJS-MHDR_-_JACK_6_35MM7.Tip_(6), DIN1.4, DIN2.4, DIN3.4, DIN4.4, DIN5.4, Part2.3.3V
  N3: AMPHENOL_-_ACJS-MHDR_-_JACK_6_35MM3.Sleeve_(4), Part2.IO27_A10, R19.Pin_0
  N4: AMPHENOL_-_ACJS-MHDR_-_JACK_6_35MM4.Sleeve_(4), Part2.IO15_A8, R20.Pin_0
  N5: AMPHENOL_-_ACJS-MHDR_-_JACK_6_35MM5.Sleeve_(4), Part2.IO14_A6, R23.Pin_0
  N6: AMPHENOL_-_ACJS-MHDR_-_JACK_6_35MM6.Sleeve_(4), Part2.SCL, R21.Pin_0
  N7: AMPHENOL_-_ACJS-MHDR_-_JACK_6_35MM7.Sleeve_(4), Part2.SDA, R22.Pin_0
  N8: DIN1.5, DIN2.5, DIN3.5, DIN4.5, DIN5.5, Part2.GND, R18.Pin_1, R19.Pin_1, R20.Pin_1, R21.Pin_1, R22.Pin_1, R23.Pin_1, LED1.common_cathode, R27.Pin_0, R28.Pin_0, R29.Pin_0, R30.Pin_0, R31.Pin_0
  N9: DIN1.2, Part2.A2_I34, R31.Pin_1
  N10: DIN2.2, Part2.A3_I39, R30.Pin_1
  N11: DIN3.2, Part2.A4_IO36, R29.Pin_1
  N12: DIN4.2, Part2.SCK, Part2.IO33_A9, R28.Pin_1
  N13: DIN5.2, Part2.MISO, Part2.IO32_A7, R27.Pin_1
  N14: Part2.A5_IO4, R25.Pin_1
  N15: Part2.A1_DAC1, R26.Pin_1
  N16: Part2.A0_DAC2, R24.Pin_1

notes:
  NB - Currently you can not use WiFi and do an analogRead on any pin below 32, i.e. use A2, A3, A4​, A7, A9
  byte buttons[] = {23, 22, 14, 15, 27, 13};
  12 - This is GPIO #12 and also an analog input A11. This pin has a pull-down resistor built into it, we recommend using it as an output only, or making sure that the pull-down is not affected during boot.
  byte faders[] = {A2, A3, A4, A9, A7};
  17 cols x 18 rows

custom parts:
  AMPHENOL - ACJS-MHDR: AMPHENOL - ACJS-MHDR - JACK, 6.35MM, PCB, STEREO)
  Lithium Ion Polymer Battery 3.7v 500mAh: Lithium ion polymer (also known as 'lipo' or 'lipoly') batteries are thin, light and powerful. The output ranges from 4.2V when completely charged to 3.7V. This battery has a capacity of 500mAh for a total of about 1.9 Wh. The batteries come pre-attached with a genuine 2-pin JST-PH connector as shown and include the necessary protection circuitry.
